# Fritzing sketch Esquematico (saved by Fritzing 0.9.3b)
breadboards: 1

parts:
  Arduino_Leonardo = Arduino Leonardo (Rev3b)
  DHT11 = KY-015 Temperature & Humidity Sensor Module [package="Breakout board"]
  R1 = Resistor [tolerance=±5% resistance=220 package=THT]
  R2 = Resistor [tolerance=±5% resistance=220 package=THT]
  LED1 = LEDs [package=led10mm]
  LED2 = LEDs [package=led10mm]

nets:
  N1: Arduino_Leonardo.D5_PWM, LED2.A
  N2: Arduino_Leonardo.D6_PWM/A7, LED1.A
  N3: Arduino_Leonardo.D7, DHT11.Vin
  N4: Arduino_Leonardo.5V, DHT11.S
  N5: Arduino_Leonardo.GND, DHT11.-, R1.Pin_1, R2.Pin_1
  N6: R1.Pin_0, LED1.C
  N7: R2.Pin_0, LED2.C

custom parts:
  KY-015 Temperature & Humidity Sensor Module: KY-015 temperature and humidity sensor module, provides a low-latency serial interface to measure humidity and temperature.
